# Fritzing sketch breadboard (saved by Fritzing 0.9.2b)
breadboards: 1

parts:
  IC1 = MCP3008 8-channel 10-bit ADC [part_number=MCP3008]
  J1 = Cobbler Plus
  T1 = TMP36 Temperature Sensor [package="TO92 [THT]"]
  U2 = RELAY-SOLIDSTATE [package=relay-s108t02]

nets:
  N1: IC1.no_name_yet#1, T1.Vout
  N2: IC1.no_name_yet#9, IC1.no_name_yet#14, J1.SCLK, T1.GND, U2.-
  N3: IC1.no_name_yet#10, J1.#6
  N4: IC1.no_name_yet#11, J1.#5
  N5: IC1.no_name_yet#12, J1.EEC
  N6: IC1.no_name_yet#13, J1.CE1
  N7: IC1.no_name_yet#15, IC1.no_name_yet#16, J1.3V3, T1.+Vs
  N8: J1.GND#5, U2.+

notes:
  Controlled appliance's power supply
  Connects to Raspberry

custom parts:
  Cobbler Plus: The Cobbler Plus is an add on prototyping board from Adafruit specifically designed for the Raspberry Pi B+ that can break out all those tasty power, GPIO, I2C and SPI pins from the 40-pin header onto a solderless breadboard. This set will make "cobbling together" prototypes with the Pi super easy. The Cobbler Plus can plug into any solderless breadboard.
